# Fritzing sketch led_basics_part_1 (saved by Fritzing 0.9.3b)
circuit board: 8.46667cm x 5.64444cm
breadboards: 1

parts:
  Part1 = Arduino Leonardo (Rev3b)
  R1 = Resistor [tolerance=±1% resistance=220 package=THT]
  LED1 = LED - 5mm [color="Red (633nm)" package="5 mm [THT]"]
  R2 = Resistor [tolerance=±1% resistance=1k package=THT]
  R3 = Resistor [tolerance=±1% resistance=10k package=THT]
  LED3 = LED - 5mm [color="Red (633nm)" package="5 mm [THT]"]
  LED2 = LED - 5mm [color="Red (633nm)" package="5 mm [THT]"]

nets:
  5V: Part1.5V, R1.Pin_0, R2.Pin_0, R3.Pin_0
  GND: Part1.GND, LED1.cathode, LED3.cathode, LED2.cathode
  N1: R1.Pin_1, LED1.anode
  N2: R2.Pin_1, LED2.anode
  N3: R3.Pin_1, LED3.anode

notes:
  Arduino Exercises, Simple LED wireing with differnt resistors, 1
