# Fritzing sketch led_basics_part_2 (saved by Fritzing 0.9.3b)
circuit board: 6.88566cm x 5.36311cm
breadboards: 1

parts:
  Part2 = Arduino Leonardo (Rev3b)
  R3 = Resistor [tolerance=±1% resistance=10k package=THT]
  LED1 = LED - 5mm [color="Red (633nm)" package="5 mm [THT]"]
  LED2 = LED - 5mm [color="Red (633nm)" package="5 mm [THT]"]
  LED3 = LED - 5mm [color="Red (633nm)" package="5 mm [THT]"]
  S2 = Pushbutton [package="[THT]"]
  S3 = Pushbutton [package="[THT]"]
  R1 = Resistor [tolerance=±1% resistance=220 package=THT]
  R2 = Resistor [tolerance=±1% resistance=1k package=THT]
  S1 = Pushbutton [package="[THT]"]

nets:
  5V: Part2.5V, R3.Pin_0, R1.Pin_0, R2.Pin_0
  GND: Part2.GND, S2.Pin_1, S3.Pin_1, S1.Pin_1
  N1: R3.Pin_1, LED3.anode
  N2: LED1.cathode, S1.Pin_3, S1.Pin_4
  N3: LED1.anode, R1.Pin_1
  N4: LED2.cathode, S2.Pin_3, S2.Pin_4
  N5: LED2.anode, R2.Pin_1
  N6: LED3.cathode, S3.Pin_3, S3.Pin_4

notes:
  Arduino Exercises, Simple LED wireing with differnt resistors and switches, 1
