# Fritzing sketch led_basics_part_3 (saved by Fritzing 0.9.3b)
circuit board: 6.88566cm x 5.36311cm
breadboards: 1

parts:
  Part2 = Arduino Leonardo (Rev3b)
  LED1 = LED - 5mm [color="Red (633nm)" package="5 mm [THT]"]
  R1 = Resistor [tolerance=±1% resistance=220 package=THT]
  R2 = Trimmer Potentiometer [maximum_resistance=10kΩ package=THT]

nets:
  5V: Part2.5V, R1.Pin_0
  GND: Part2.GND, LED1.cathode
  N1: LED1.anode, R2.wiper
  N2: R1.Pin_1, R2.leg2

notes:
  Arduino Exercises, Simple LED wireing with differnt resistors and switches, 1
